# Fritzing sketch ADCinterrupts_potDrivesServo (saved by Fritzing 0.8.3b)
breadboards: 1

parts:
  Part1 = Arduino Uno (Rev3)
  U1 = POT [package=pot_mammoth]
  C1 = Electrolytic Capacitor [capacitance=1µF package="100 mil [THT, electrolytic]"]
  J1 = Basic Servo

nets:
  N1: Part1.A0, U1.A, C1.+
  GND: Part1.GND, U1.E, C1.-, J1.gnd
  N2: Part1.D9_PWM, J1.pulse
  5V: Part1.5V, U1.S, J1.vcc

notes:
  I'm using 0.1uf
