# Fritzing sketch StepperMotor_w2803 (saved by Fritzing 0.8.3b)
breadboards: 1

parts:
  Part1 = Arduino Uno (Rev3)
  IC1 = ULN2803A [package=THT]
  M1 = Stepper Motor - Unipolar

nets:
  N1: Part1.GND, IC1.0V
  N2: Part1.D9_PWM, IC1.In_4
  N3: Part1.D3_PWM, IC1.In_1
  N4: Part1.D5_PWM, IC1.In_2
  N5: Part1.D7, IC1.In_3
  N6: IC1.COM_-_Common, M1.A
  N7: IC1.Out_4, M1.D
  N8: IC1.Out_3, M1.COMMON_2
  N9: IC1.Out_2, M1.B
  N10: IC1.Out_1, M1.C

notes:
  Color coding of 24BYJ48 5-Wire stepper motor I used matches what I have coming from UNO -
  RedOrangeYellowPupleBlack - where Red is COM(12V)
  External 12V Power Supply
